// Digital circuit UTS NO.11.dig as structural Verilog
module UTS_NO_11 (
  input  X,
  input  Y,
  input  Z
);

  wire and_1_out, and_2_out, and_3_out, and_4_out, not_1_out, not_2_out, not_3_out, not_4_out, or_1_out;

  and and_1 (and_1_out, not_1_out, not_2_out, Z);
  not not_1 (not_1_out, X);
  not not_2 (not_2_out, Y);
  and and_2 (and_2_out, X, Y, not_3_out);
  not not_3 (not_3_out, Z);
  and and_3 (and_3_out, not_4_out, Y, Z);
  not not_4 (not_4_out, X);
  and and_4 (and_4_out, X, Y);
  or or_1 (or_1_out, and_1_out, and_2_out, and_3_out, and_4_out);
  LED u_X (.in(or_1_out));

  // Notes on the sheet:
  //   X'Y'Z+XYZ'+X'YZ+XY
  //   IKBAR SHAFAR ROBBANI
  //   NIM : 213050035
endmodule
