// Digital circuit UTS NO.12.dig as structural Verilog
module UTS_NO_12 (
  input  X,
  input  Y,
  input  Z
);

  wire and_1_out, and_2_out, and_3_out, not_1_out, not_2_out, not_3_out, or_1_out;

  not not_1 (not_1_out, Z);
  not not_2 (not_2_out, Y);
  not not_3 (not_3_out, Z);
  and and_1 (and_1_out, X, Y, not_1_out);
  and and_2 (and_2_out, not_2_out, not_3_out);
  and and_3 (and_3_out, X, Z);
  or or_1 (or_1_out, and_1_out, and_2_out, and_3_out);
  LED led_1 (.in(or_1_out));

  // Notes on the sheet:
  //   XYZ'+Y'Z'+XZ
  //   IKBAR SHAFAR ROBBANI
  //   NIM : 213050035
endmodule
