// Digital circuit UTS NO.13.dig as structural Verilog
module UTS_NO_13 (
  input  X,
  input  Y,
  input  Z
);

  wire and_1_out, and_2_out, and_3_out, not_1_out, not_2_out, not_3_out, or_1_out;

  and and_1 (and_1_out, not_1_out, Y, Z);
  not not_1 (not_1_out, X);
  and and_2 (and_2_out, X, not_2_out);
  not not_2 (not_2_out, Y);
  and and_3 (and_3_out, Y, not_3_out);
  not not_3 (not_3_out, Z);
  or or_1 (or_1_out, and_1_out, and_2_out, and_3_out);
  LED O (.in(or_1_out));

  // Notes on the sheet:
  //   X'YZ+XY'+YZ'
  //   IKBAR SHAFAR ROBBANI
  //   NIM : 213050035
endmodule
