// Digital circuit UTS NO.4.dig as structural Verilog
module UTS_NO_4 (
  input  A,
  input  B,
  input  C,
  input  D
);

  wire and_1_out, and_2_out, and_3_out, not_1_out, not_2_out, not_3_out, not_4_out, or_1_out;

  and and_1 (and_1_out, not_1_out, B);
  not not_1 (not_1_out, A);
  and and_2 (and_2_out, not_2_out, not_3_out, not_4_out);
  not not_2 (not_2_out, A);
  not not_3 (not_3_out, B);
  not not_4 (not_4_out, C);
  and and_3 (and_3_out, C, D);
  or or_1 (or_1_out, and_1_out, and_2_out, and_3_out);
  LED X (.in(or_1_out));

  // Notes on the sheet:
  //   IKBAR SHAFAR ROBBANI
  //   NIM : 213050035
  //   A'B + A'B'C' + CD = X
endmodule
