// Digital circuit UTS NO.8.dig as structural Verilog
module UTS_NO_8 (
  input  A,
  input  B,
  input  C,
  input  D
);

  wire and_1_out, and_2_out, and_3_out, and_4_out, and_5_out, not_1_out, not_2_out, not_3_out, or_1_out;

  and and_1 (and_1_out, not_1_out, B, not_2_out);
  not not_1 (not_1_out, A);
  not not_2 (not_2_out, D);
  and and_2 (and_2_out, B, D, C);
  and and_3 (and_3_out, A, D, not_3_out);
  not not_3 (not_3_out, C);
  and and_4 (and_4_out, B, D);
  and and_5 (and_5_out, A, B, C);
  or or_1 (or_1_out, and_1_out, and_2_out, and_3_out, and_4_out, and_5_out);
  LED X (.in(or_1_out));

  // Notes on the sheet:
  //   A'BD'+BDC+ABC'+BD+ABC
  //   IKBAR SHAFAR ROBBANI
  //   NIM : 213050035
endmodule
